# Fritzing sketch atmoscan_schema (saved by Fritzing 0.9.3b)
breadboards: 1

parts:
  Componente1 = Arduino Nano (Rev3.0)
  Componente2 = Real Time Clock Module - DS1307 RTC Breakout Board
  Componente3 = MicroSD Card Module
  DHT1 = DHT11 Humitidy and Temperature Sensor
  Power_plug1 = Power plug
  J1 = Piezo Speaker

nets:
  GND: Componente1.GND, Componente2.GND, Componente3.GND, DHT1.GND, Power_plug1.GND, J1.pin1
  N1: Componente1.D2, J1.pin2
  N2: Componente1.D3, DHT1.DATA
  N3: Componente1.D8, Componente3.CS
  N4: Componente1.D11/MOSI, Componente3.MOSI
  N5: Componente1.D12/MISO, Componente3.MISO
  5V: Componente1.5V, Componente2.5V, Componente3.VCC, DHT1.VDD
  N6: Componente1.A5, Componente2.SCL
  N7: Componente1.A4, Componente2.SDA
  N8: Componente1.D13/SCK, Componente3.SCK

custom parts:
  DHT11 Humitidy and Temperature Sensor: DHT11 Humidity and Temperature Sensor
